# Fritzing sketch Mini Cube Breadboard (saved by Fritzing 0.9.3b)
perfboards: 1

parts:
  J1 = Piezo Speaker
  RCWL-0516_Microwave_Radar_Motion_Sensor1 = RCWL-0516 Microwave Radar Motion Sensor Module
  Nano1 = Arduino Nano v2.3
  R20 = Resistor [tolerance=±5% resistance=1M package="2512 [SMD]"]
  Part1 = ws2812b [package="smd 2812b"]
  R21 = Resistor [tolerance=±5% resistance=330 package="2010 [SMD]"]

nets:
  N1: J1.pin1, RCWL-0516_Microwave_Radar_Motion_Sensor1.GND
  N2: J1.pin2, R20.Pin_0, R20.Pin_1
  VIN: RCWL-0516_Microwave_Radar_Motion_Sensor1.VIN, Part1.VDD
  N3: Nano1.D2, R21.Pin_1
  N4: Part1.DIN, R21.Pin_0

custom parts:
  RCWL-0516 Microwave Radar Motion Sensor Module: The RCWL-0516 is a microwave radar motion sensor module. Input voltage is 4V to 28V. The 3V3 pin is a power output.
